# Fritzing sketch cryptopi (saved by Fritzing 0.9.3b)
breadboards: 2

parts:
  Raspberry_Pi_1 = Raspberry Pi 3 [part_number=RPI-3-V1.2]  # not connected
  LCD1 = LCD screen  # not connected
  PIR1 = PIR sensor  # not connected
  S2 = Momentary Switch [package=ksa_sealed_tac_switch]
  S3 = Momentary Switch [package=ksa_sealed_tac_switch]  # not connected
  S4 = Momentary Switch [package=ksa_sealed_tac_switch]
  S5 = Momentary Switch [package=ksa_sealed_tac_switch]
  S6 = Momentary Switch [package=ksa_sealed_tac_switch]
  7_Segment1 = 7 Segment Display
  7_Segment3 = 7 Segment Display
  Q1 = NPN-Transistor [package="TO92 [THT]"]  # not connected
  Q2 = NPN-Transistor [package="TO92 [THT]"]
  R3 = Resistor [tolerance=±5% resistance=1k package=THT]
  R4 = Resistor [tolerance=±5% resistance=1k package=THT]
  R5 = Resistor [tolerance=±5% resistance=1k package=THT]
  R6 = Resistor [tolerance=±5% resistance=1k package=THT]
  R7 = Resistor [tolerance=±5% resistance=1k package=THT]
  R8 = Resistor [tolerance=±5% resistance=1k package=THT]
  R9 = Resistor [tolerance=±5% resistance=1k package=THT]
  R10 = Resistor [tolerance=±5% resistance=10k package=THT]
  R11 = Resistor [tolerance=±5% resistance=10k package=THT]
  LED1 = LED - 5mm [color="Red (633nm)" package="5 mm [THT]"]
  LED2 = LED - 5mm [color="Green (570nm)" package="5 mm [THT]"]  # not connected

nets:
  N1: S2.1, S2.2
  N2: S2.3, S2.4
  N3: S4.1, S4.2
  N4: S4.3, S4.4
  N5: S5.1, S5.2
  N6: S5.3, S5.4
  N7: S6.1, S6.2
  N8: S6.3, S6.4
  N9: 7_Segment1.Segment_A#1, 7_Segment1.Segment_F
  N10: 7_Segment1.Segment_B, 7_Segment1.Segment_A#10
  N11: 7_Segment3.Segment_A#1, 7_Segment3.Segment_F
  N12: 7_Segment3.Segment_B, 7_Segment3.Segment_A#10
  N13: Q2.E, LED1.anode
  N14: R3.Pin_0, R7.Pin_0, R8.Pin_0, R9.Pin_0
  N15: R3.Pin_1, R7.Pin_1, R8.Pin_1, R9.Pin_1
  N16: R4.Pin_0, R5.Pin_0, R6.Pin_0
  N17: R4.Pin_1, R5.Pin_1, R6.Pin_1
  N18: R10.Pin_0, R10.Pin_1
  N19: R11.Pin_0, R11.Pin_1
